# Fritzing sketch 1 (saved by Fritzing 0.9.5d)
breadboards: 1

parts:
  パーツ1 = Arduino Uno (Rev3)
  R2 = Resistor [tolerance=±5% resistance=10k package=THT]
  パーツ2 = LSM303C (6 DOF)  # not connected
  R1 = Basic Flex Resistor

nets:
  N1: パーツ1.A0, R2.Pin_1, R1.Pin_2
  N2: パーツ1.5V, R2.Pin_0
  N3: パーツ1.GND, R1.pin_1
